# Fritzing sketch satcom-relay (saved by Fritzing 0.9.9b)

parts:
  Part3 = Adafruit FeatherWing Proto [part_number="Adafruit #2884"]
  Part5 = Adafruit Feather M0 Basic Proto [part_number="Adafruit #2772"]
  Part2 = Adafruit GPS FeatherWing [part_number="Adafruit #3133"]
  J1 = female pin header, 10 pins [form="♀ (female)"]
  Part6 = Lithium Ion Polymer Battery 3.7v 2500mAh [part_number=328]  # not connected
  Part7 = Adafruit FeatherWing Doubler [part_number="Adafruit #2890"]
  Part8 = Adafruit FeatherWing Doubler [part_number="Adafruit #2890"]
  Part11 = Adafruit Feather M0 Adalogger [part_number="Adafruit #2796"]
  Part12 = Adafruit Feather M0 RFM9x LoRa [part_number="Adafruit #3178 or #3179"]

nets:
  N1: Part3.G, J1.pin1
  N2: Part3.RX, J1.pin9, J1.pin10
  N3: Part3.C, J1.pin4
  N4: Part3.D, Part3.TX, J1.pin5, J1.pin6
  N5: Part3.E, J1.pin7
  N6: Part3.VBAT, J1.pin2, J1.pin3
  GND: Part5.GND, Part2.GND, Part2.G, Part8.G, Part8.GND
  N7: Part5.D1, Part2.TX, Part8.TX
  N8: Part5.D0, Part2.RX, Part8.RX
  N9: Part5.MISO, Part2.MISO, Part8.MISO
  N10: Part5.MOSI, Part2.MOSI, Part8.MOSI
  N11: Part5.SCK, Part2.SCK, Part8.SCK
  N12: Part5.A5, Part2.F, Part8.F
  N13: Part5.A4, Part2.E, Part8.E
  N14: Part5.A3, Part2.D, Part8.D
  N15: Part5.A2, Part2.C, Part8.C
  N16: Part5.A1, Part2.B, Part8.B
  N17: Part5.A0, Part2.ENABLE, Part2.A, Part8.A
  N18: Part5.AREF, Part2.AREF, Part8.AREF
  N19: Part5.+3V3, Part2.3V, Part8.3V
  N20: Part5.!RESET, Part2.RST, Part8.RESET
  N21: Part5.VBAT, Part2.VBAT, Part8.VBAT
  N22: Part5.EN, Part2.EN, Part8.EN
  N23: Part5.VBUS, Part2.USB, Part8.USB
  N24: Part5.D13, Part2.N, Part8.O
  N25: Part5.D12, Part2.M, Part8.N
  N26: Part5.D11, Part2.L, Part8.M
  N27: Part5.D10, Part2.K, Part8.L
  N28: Part5.D9, Part2.J, Part8.K
  N29: Part5.D6, Part2.I, Part8.J
  N30: Part5.D5, Part2.H, Part8.I
  N31: Part5.SCL, Part2.SCL, Part8.SCL
  N32: Part5.SDA, Part2.SDA, Part8.SDA
  +3V3: Part7.3V, Part11.+3V3, Part12.+3V3
  N33: Part7.RESET, Part11.!RESET
  N34: Part7.F, Part11.A5
  N35: Part7.G, Part11.GND, Part12.DIO1
  N36: Part7.L, Part11.D10
  N37: Part7.M, Part11.D11
  N38: Part7.VBAT, Part11.VBAT
  N39: Part7.B, Part12.A1
  N40: Part7.MISO, Part12.D0
  N41: Part7.I, Part12.D1

custom parts:
  Adafruit FeatherWing Proto: This is the FeatherWing Proto - a prototyping add-on for all Feather boards. Using our Feather Stacking Headers or Feather Female Headers you can connect a FeatherWing on top or bottom of your Feather board and let the board take flight! This has a duplicate breakout for each pin on a Feather, as well as a bunch of plain grid proto holes. For GND and 3.3V, we give you a strip of connected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
  Adafruit Feather M0 Basic Proto: At the Feather M0's heart is an ATSAMD21G18 ARM Cortex M0 processor, clocked at 48 MHz and at 3.3V logic, the same one used in the new Arduino Zero. This chip has a whopping 256K of FLASH (8x more than the Atmega328 or 32u4) and 32K of RAM (16x as much)! This chip comes with built in USB so it has USB-to-Serial program & debug capability built in with no need for an FTDI-like chip. To make it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
  Adafruit GPS FeatherWing: Give your Feather a sense of place, with an Ultimate GPS FeatherWing. In 2013 we designed the Ultimate GPS module to satisfy all your GPS desires - and now we have brought its power and versatility plus more to our Feather series with the Adafruit Ultimate GPS FeatherWing! This FeatherWing plugs right into your Feather board and gives it a precise, sensitive, and low power GPS module for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
  Lithium Ion Polymer Battery 3.7v 2500mAh: Lithium ion polymer (also known as 'lipo' or 'lipoly') batteries are thin, light and powerful. The output ranges from 4.2V when completely charged to 3.7V. This battery has a capacity of 2500mAh for a total of about 10 Wh. The batteries come pre-attached with a genuine 2-pin JST-PH connector as shown and include the necessary protection circuitry.
  Adafruit FeatherWing Doubler: This is the FeatherWing Doubler - a prototyping add-on and more for all Feather boards. This is similar to our FeatherWing Proto except there are two! The magic of the Doubler comes when stacking a Feather and another board on top of the Doubler so you can work with both boards simultaneously side-by-side! The Doubler, like the Proto, has a duplicate breakout for each pin on a Feather, as well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
  Adafruit Feather M0 Adalogger: This is the Adafruit Feather M0 Adalogger - our take on an 'all-in-one' Cortex M0 datalogger (or data-reader) with built in USB and battery charging. Its an Adafruit Feather M0 with a microSD holder ready to rock! We have other boards in the Feather family, check'em out here At the Feather M0's heart is an ATSAMD21G18 ARM Cortex M0 processor, clocked at 48 MHz and at 3.3V logic, the same one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
  Adafruit Feather M0 RFM9x LoRa: This is the Adafruit Feather M0 RFM95 LoRa Radio - our take on an microcontroller with a "Long Range (LoRa)" packet radio transceiver with built in USB and battery charging. Its an Adafruit Feather M0 with a 433Mhz or 900MHz radio module cooked in! Great for making wireless networks that are more flexible than Bluetooth LE and without the high power requirements of WiFi. We have other boards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
